# Fritzing sketch Joystick PS2 (saved by Fritzing 0.9.1b)

parts:
  module1 = JoyStick
  元件1 = SunFounder Uno R3

nets:
  GND: module1.GND, 元件1.GND
  VCC: module1.VCC, 元件1.5V
  N1: module1.BT, 元件1.D7
  N2: module1.X, 元件1.A0
  N3: module1.Y, 元件1.A1

notes:
  Joystick PS2

custom parts:
  JoyStick: JoyStick module of SunFounder Sensor Kit
  SunFounder Uno R3: The Arduino Uno is a microcontroller board based on the ATmega328 (datasheet). It has 14 digital input/output pins (of which 6 can be used as PWM outputs), 6 analog inputs, a 16 MHz ceramic resonator, a USB connection, a power jack, an ICSP header, and a reset button. It contains everything needed to support the microcontroller; simply connect it to a computer with a USB cable or power it with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
