# Fritzing sketch Vibration Switch (saved by Fritzing 0.9.1b)

parts:
  module4 = Vibration Switch
  元件1 = SunFounder Uno R3

nets:
  N1: module4.SIG, 元件1.D8
  GND: module4.GND, 元件1.GND
  VCC: module4.VCC, 元件1.5V

notes:
  Vibration Switch

custom parts:
  SunFounder Uno R3: The Arduino Uno is a microcontroller board based on the ATmega328 (datasheet). It has 14 digital input/output pins (of which 6 can be used as PWM outputs), 6 analog inputs, a 16 MHz ceramic resonator, a USB connection, a power jack, an ICSP header, and a reset button. It contains everything needed to support the microcontroller; simply connect it to a computer with a USB cable or power it with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
