# Fritzing sketch Photoresistor Sensor (saved by Fritzing 0.9.1b)

parts:
  module1 = Photoresistor
  module2 = Relay Module
  元件1 = SunFounder Uno R3

nets:
  N1: module1.SIG, 元件1.A0
  GND: module1.GND, module2.GND, 元件1.GND
  VCC: module1.VCC, module2.VCC, 元件1.5V
  N2: module2.SIG, 元件1.D8

notes:
  Photoresister
  relay

custom parts:
  Photoresistor: Photoresistor module of SunFounder Sensor Kit
  Relay Module: Relay Module of SunFounder Sensor Kit
  SunFounder Uno R3: The Arduino Uno is a microcontroller board based on the ATmega328 (datasheet). It has 14 digital input/output pins (of which 6 can be used as PWM outputs), 6 analog inputs, a 16 MHz ceramic resonator, a USB connection, a power jack, an ICSP header, and a reset button. It contains everything needed to support the microcontroller; simply connect it to a computer with a USB cable or power it with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
