# Fritzing sketch RGB LED (saved by Fritzing 0.8.7b)

parts:
  module1 = RGB LED
  元件2 = SunFounder Uno R3

nets:
  N1: module1.R, 元件2.D11_PWM/MOSI
  N2: module1.G, 元件2.D10_PWM/SS
  VCC: module1.VCC, 元件2.5V
  N3: module1.B, 元件2.D9_PWM

notes:
  RGB LED

custom parts:
  RGB LED: RGB LED module of SunFounder Sensor Kit
  SunFounder Uno R3: The SunFounder Uno is a microcontroller board based on the ATmega328 (datasheet). It has 14 digital input/output pins (of which 6 can be used as PWM outputs), 6 analog inputs, a 16 MHz ceramic resonator, a USB connection, a power jack, an ICSP header, and a reset button. It contains everything needed to support the microcontroller; simply connect it to a computer with a USB cable or power it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
