# Fritzing sketch Dual-color LED (saved by Fritzing 0.9.1b)

parts:
  module1 = Double Color LED
  元件1 = SunFounder Uno R3

nets:
  N1: module1.G, 元件1.D10_PWM/SS
  GND: module1.GND, 元件1.GND
  N2: module1.R, 元件1.ICSP_MOSI, 元件1.D11_PWM/MOSI

notes:
  Dual-color LED

custom parts:
  Double Color LED: Double color LED module of SunFounder Sensor Kit
  SunFounder Uno R3: The Arduino Uno is a microcontroller board based on the ATmega328 (datasheet). It has 14 digital input/output pins (of which 6 can be used as PWM outputs), 6 analog inputs, a 16 MHz ceramic resonator, a USB connection, a power jack, an ICSP header, and a reset button. It contains everything needed to support the microcontroller; simply connect it to a computer with a USB cable or power it with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
