# Fritzing sketch Rotary Encoder (saved by Fritzing 0.9.1b)

parts:
  module1 = Rotary Encoder
  元件1 = SunFounder Uno R3

nets:
  N1: module1.CLK, 元件1.D2
  N2: module1.DT, 元件1.D3_PWM
  VCC: module1.VCC, 元件1.5V
  GND: module1.GND, 元件1.GND
  N3: module1.SW, 元件1.D4

notes:
  Rotary Encoder

custom parts:
  Rotary Encoder: Rotary Encoder module of SunFounder Sensor Kit
  SunFounder Uno R3: The Arduino Uno is a microcontroller board based on the ATmega328 (datasheet). It has 14 digital input/output pins (of which 6 can be used as PWM outputs), 6 analog inputs, a 16 MHz ceramic resonator, a USB connection, a power jack, an ICSP header, and a reset button. It contains everything needed to support the microcontroller; simply connect it to a computer with a USB cable or power it with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
