# Fritzing sketch color sensor (saved by Fritzing 0.9.1b)

parts:
  module1 = Color Seneor
  元件1 = SunFounder Uno R3

nets:
  N1: module1.S0, 元件1.D3_PWM
  N2: module1.S1, 元件1.D4
  N3: module1.S2, 元件1.D5_PWM
  N4: module1.S3, 元件1.D6_PWM
  N5: module1.OUT, 元件1.D2
  VCC: module1.VCC, 元件1.5V
  GND: module1.GND, 元件1.GND

notes:
  color sensor

custom parts:
  Color Seneor: Color Sensor of SunFounder Sensor Kit for Arduino
  SunFounder Uno R3: The Arduino Uno is a microcontroller board based on the ATmega328 (datasheet). It has 14 digital input/output pins (of which 6 can be used as PWM outputs), 6 analog inputs, a 16 MHz ceramic resonator, a USB connection, a power jack, an ICSP header, and a reset button. It contains everything needed to support the microcontroller; simply connect it to a computer with a USB cable or power it with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
