# Fritzing sketch AD DA Converter PCF8591 (saved by Fritzing 0.9.1b)

parts:
  module1 = PCF8591
  元件1 = SunFounder Uno R3

nets:
  N1: module1.AO, 元件1.D13/SCK
  VCC: module1.VCC, 元件1.5V
  GND: module1.GND, 元件1.GND
  N2: module1.SDA, 元件1.A4/SDA
  N3: module1.SCL, 元件1.A5/SCL

notes:
  AD/DA Converter PCF8591

custom parts:
  PCF8591: PCF8591 ADC module for SunFounder Sensor Kit
  SunFounder Uno R3: The Arduino Uno is a microcontroller board based on the ATmega328 (datasheet). It has 14 digital input/output pins (of which 6 can be used as PWM outputs), 6 analog inputs, a 16 MHz ceramic resonator, a USB connection, a power jack, an ICSP header, and a reset button. It contains everything needed to support the microcontroller; simply connect it to a computer with a USB cable or power it with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
