# Fritzing sketch Raindrop Sensor (saved by Fritzing 0.9.1b)

parts:
  module1 = Rain Detection board
  module2 = LM393
  元件1 = SunFounder Uno R3

nets:
  N1: module1.+, module2.GND#10
  N2: module1.-, module2.IN
  N3: module2.AO, 元件1.A0
  N4: module2.DO, 元件1.D7
  VCC: module2.VCC, 元件1.5V
  N5: module2.GND#8, 元件1.GND

notes:
  Raindrop sensor analyser
  Raindrop Sensor

custom parts:
  Rain Detection board: Rain Detection board for SunFounder Sensor Kit (along with LM393).
  LM393: LM393 module of SunFounder Sensor Kit
  SunFounder Uno R3: The Arduino Uno is a microcontroller board based on the ATmega328 (datasheet). It has 14 digital input/output pins (of which 6 can be used as PWM outputs), 6 analog inputs, a 16 MHz ceramic resonator, a USB connection, a power jack, an ICSP header, and a reset button. It contains everything needed to support the microcontroller; simply connect it to a computer with a USB cable or power it with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
