# Fritzing sketch Thermostatic Water Tank (saved by Fritzing 0.9.1b)
breadboards: 1

parts:
  module1 = Relay Module
  module2 = I2C LCD1602
  module3 = Button
  module4 = Analog Thermistor
  module5 = Rotary Encoder
  元件1 = SunFounder Uno R3

nets:
  N1: module1.SIG, 元件1.D2
  VCC: module1.VCC, module2.VCC, module3.VCC, module4.VCC, module5.VCC, 元件1.5V
  GND: module1.GND, module2.GND, module3.GND, module4.GND, module5.GND, 元件1.GND
  N2: module2.SCL, 元件1.A5/SCL
  N3: module2.SDA, 元件1.A4/SDA
  N4: module3.SIG, 元件1.D10_PWM/SS
  N5: module4.SIG, 元件1.A0
  N6: module5.CLK, 元件1.D7
  N7: module5.DT, 元件1.D6_PWM
  N8: module5.SW, 元件1.D5_PWM

notes:
  Thermistor
  Button
  Rotary Encoder
  Relay
  I2C LCD1602

custom parts:
  Relay Module: Relay Module of SunFounder Sensor Kit
  I2C LCD1602: I2C LCD1602 module of SunFounder Sensor Kit
  Button: Button module of SunFounder Sensor Kit
  Analog Thermistor: Analog Thermistor module of SunFounder Sensor Kit
  Rotary Encoder: Rotary Encoder module of SunFounder Sensor Kit
  SunFounder Uno R3: The Arduino Uno is a microcontroller board based on the ATmega328 (datasheet). It has 14 digital input/output pins (of which 6 can be used as PWM outputs), 6 analog inputs, a 16 MHz ceramic resonator, a USB connection, a power jack, an ICSP header, and a reset button. It contains everything needed to support the microcontroller; simply connect it to a computer with a USB cable or power it with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
