# Fritzing sketch Real-time Clock Module (saved by Fritzing 0.9.1b)

parts:
  module1 = DS1302 RTC
  module2 = I2C LCD1602
  元件1 = SunFounder Uno R3

nets:
  N1: module1.SCL, 元件1.D7
  N2: module1.SDA, 元件1.D6_PWM
  VCC: module1.VCC, module2.VCC, 元件1.5V
  GND: module1.GND, module2.GND, 元件1.GND
  N3: module1.RST, 元件1.D5_PWM
  N4: module2.SCL, 元件1.A5/SCL
  N5: module2.SDA, 元件1.A4/SDA

notes:
  DS1302

custom parts:
  DS1302 RTC: DS1302RTC module of SunFounder Sensor Kit
  I2C LCD1602: I2C LCD1602 module of SunFounder Sensor Kit
  SunFounder Uno R3: The Arduino Uno is a microcontroller board based on the ATmega328 (datasheet). It has 14 digital input/output pins (of which 6 can be used as PWM outputs), 6 analog inputs, a 16 MHz ceramic resonator, a USB connection, a power jack, an ICSP header, and a reset button. It contains everything needed to support the microcontroller; simply connect it to a computer with a USB cable or power it with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
